// Digital circuit MITE_May15_1.dig as structural Verilog
module MITE_May15_1 (
  input  in_1,
  input  in_2,
  input  clk_2,
  output CLK,
  output T9,
  output T1,
  output T0,
  output GCLK,
  output nPH0,
  output nPH1,
  output nWR,
  output Sum,
  output Carry
);

  wire A0, A1, A2, A3, A4, A5, A6, A7, A8, A9, A10, A11, A12, A13, A14, A15, ACLK, ADD, AND, and_2_out, Aout,
       Bout, BUS0, BUS1, BUS2, BUS3, BUS4, BUS5, BUS6, BUS7, C, Cin, CLA, CLR, D__gt_A, DAT0, DAT1, DAT2,
       DAT3, DAT4, DAT5, DAT6, DAT7, diodebackward_1_out, diodebackward_6_out, diodebackward_8_out, F, GATE,
       I0, I1, IR0, IR1, IR2, IR3, IR4, IR5, IR6, IR7, JMP, LD, LOAD, MR, nA, nACOE, nADD_REG, nand_5_out,
       nand_8_out, nand_9_out, nand_10_out, nand_11_out, nand_12_out, nand_13_out, nB, nCLRPC, nD__gt_A,
       nINC_LD, nJMP, nor_4_out, not_1_out, not_4_out, not_8_out, nT1, OR, PL0, PL1, PL2, PL3, PL4, PL5, PL6,
       PL7, pullup_7_out, pullup_9_out, pullup_12_out, pullup_13_out, RA0, RA1, RA2, RA3, RD_CLK, ResC,
       SetC_t, ST, SUB, T2, T3, T4, T5, T6, T7, T8, U3_pin10, U4_pin10, U5_pin10, U7_pin12, U7_pin13,
       U7_pin14, U7_pin15, U7_pin16, U7_pin17, U7_pin18, U7_pin19, U20_pin9, U20_pin10, U20_pin11, U20_pin12,
       U20_pin13, U20_pin14, U20_pin15, U25_p21, U25_p23, XOR, xor_1_out, xor_2_out, xor_3_out, xor_4_out,
       ZERO, Zin;

  not not_1 (not_1_out, in_1);
  _744017 U1 (
    .pin1(T5), .pin2(T1), .pin3(T0), .pin4(T2), .pin5(T6), .pin6(T7), .pin7(T3), .pin8(1'b0), .pin9(T8),
    .pin10(T4), .pin11(T9), .pin13(1'b0), .pin14(clk_2), .pin15(MR), .pin16(1'b1));  // open: pin12
  _74157 U12 (
    .pin1(nADD_REG), .pin2(nPH0), .pin3(IR0), .pin4(RA0), .pin5(A1), .pin6(IR1), .pin7(RA1), .pin8(1'b0),
    .pin9(RA2), .pin10(IR2), .pin11(A2), .pin12(RA3), .pin13(IR3), .pin14(A3), .pin15(1'b0), .pin16(1'b1));
  _74574 U13 (
    .pin1(not_1_out), .pin2(BUS7), .pin3(BUS6), .pin4(BUS5), .pin5(BUS4), .pin6(BUS3), .pin7(BUS2),
    .pin8(BUS1), .pin9(BUS0), .pin10(1'b0), .pin11(D__gt_A), .pin12(A0), .pin13(A1), .pin14(A2), .pin15(A3),
    .pin16(A4), .pin17(A5), .pin18(A6), .pin19(A7), .pin20(1'b1));
  not not_2 (nINC_LD, in_2);
  not not_3 (MR, nCLRPC);
  Reset reset_1 (.out(nCLRPC));
  not not_4 (not_4_out, clk_2);
  not not_5 (nACOE, T9);
  not not_6 (nT1, T1);
  not not_7 (LD, T0);
  nand nand_1 (nPH0, T0, clk_2);
  nand nand_2 (nPH1, T0, not_4_out);
  nor nor_1 (RD_CLK, LD, clk_2);
  nor nor_2 (GCLK, GATE, clk_2);
  nor nor_3 (GATE, T0, nor_4_out);
  nor nor_4 (nor_4_out, GATE, T9);
  // _28c256 U25: pin names not known; wires that end beside it: A13, A11, A6, A5, A4, A3, A2, A1, A0, nPH0, BUS0, BUS1, BUS2, 1'b0, 1'b1, nWR, A12, A7, A8, A10, U25_p21, A9, U25_p23, BUS7
  PullUp pullup_1 (.out(nWR));
  PullUp pullup_2 (.out(U25_p21));
  or or_1 (nADD_REG, IR3, IR2, IR1, IR0);
  nand nand_3 (nWR, T9, clk_2);
  and and_1 (ACLK, clk_2, T9);
  nor nor_5 (U25_p21, T1, T0);
  nor nor_6 (U25_p23, T1, T9, T0);
  _74574 U7 (
    .pin1(1'b0), .pin2(BUS7), .pin3(BUS6), .pin4(BUS5), .pin5(BUS4), .pin6(BUS3), .pin7(BUS2), .pin8(BUS1),
    .pin9(BUS0), .pin10(1'b0), .pin11(nPH1), .pin12(U7_pin12), .pin13(U7_pin13), .pin14(U7_pin14),
    .pin15(U7_pin15), .pin16(U7_pin16), .pin17(U7_pin17), .pin18(U7_pin18), .pin19(U7_pin19), .pin20(1'b1));
  _74161 U3 (
    .pin1(nCLRPC), .pin2(clk_2), .pin3(1'b0), .pin4(1'b0), .pin5(1'b0), .pin6(1'b0), .pin7(nCLRPC),
    .pin8(1'b0), .pin9(1'b1), .pin10(U3_pin10), .pin11(A15), .pin12(A14), .pin13(A13), .pin14(A12),
    .pin16(1'b1));  // open: pin15
  _74161 U5 (
    .pin1(nCLRPC), .pin2(clk_2), .pin3(1'b0), .pin4(1'b0), .pin5(1'b0), .pin6(1'b0), .pin7(nCLRPC),
    .pin8(1'b0), .pin9(1'b1), .pin10(U5_pin10), .pin11(A11), .pin12(A10), .pin13(A9), .pin14(A8),
    .pin15(U3_pin10), .pin16(1'b1));
  PullDown pulldown_1 (.out(IR4));
  not not_8 (not_8_out, clk_2);
  _74574 U8 (
    .pin1(1'b0), .pin2(U7_pin19), .pin3(U7_pin18), .pin4(U7_pin17), .pin5(U7_pin16), .pin6(U7_pin15),
    .pin7(U7_pin14), .pin8(U7_pin13), .pin9(U7_pin12), .pin10(1'b0), .pin11(nPH0), .pin12(DAT0),
    .pin13(DAT1), .pin14(DAT2), .pin15(DAT3), .pin16(DAT4), .pin17(DAT5), .pin18(DAT6), .pin19(DAT7),
    .pin20(1'b1));
  PullUp pullup_3 (.out(IR3));
  PullUp pullup_4 (.out(IR2));
  PullUp pullup_5 (.out(IR1));
  PullUp pullup_6 (.out(IR0));
  and and_2 (and_2_out, T1, IR7, not_8_out);
  and and_3 (D__gt_A, T1, IR7, clk_2);
  _74161 U4 (
    .pin1(nCLRPC), .pin2(T0), .pin3(1'b0), .pin4(1'b0), .pin5(1'b0), .pin6(1'b0), .pin7(nCLRPC), .pin8(1'b0),
    .pin9(1'b1), .pin10(U4_pin10), .pin11(A7), .pin12(A6), .pin13(A5), .pin14(A4), .pin15(U5_pin10),
    .pin16(1'b1));
  _74161 U6 (
    .pin1(nCLRPC), .pin2(T0), .pin3(1'b0), .pin4(1'b0), .pin5(1'b0), .pin6(1'b0), .pin7(nCLRPC), .pin8(1'b0),
    .pin9(1'b1), .pin10(1'b1), .pin11(A3), .pin12(A2), .pin13(A1), .pin14(A0), .pin15(U4_pin10), .pin16(1'b1));
  _74574 U9 (
    .pin1(1'b0), .pin2(BUS7), .pin3(BUS6), .pin4(BUS5), .pin5(BUS4), .pin6(BUS3), .pin7(BUS2), .pin8(BUS1),
    .pin9(BUS0), .pin10(1'b0), .pin11(nPH0), .pin12(IR0), .pin13(IR1), .pin14(IR2), .pin15(IR3), .pin16(IR4),
    .pin17(IR5), .pin18(IR6), .pin19(IR7), .pin20(1'b1));
  not not_9 (nD__gt_A, D__gt_A);
  LED led_1 (.in(T9));
  LED led_2 (.in(T8));
  LED led_3 (.in(T7));
  LED led_4 (.in(T6));
  LED led_5 (.in(T5));
  LED led_6 (.in(T4));
  LED led_7 (.in(T3));
  LED led_8 (.in(T2));
  LED led_9 (.in(T1));
  LED led_10 (.in(T0));
  LED u_A0 (.in(nPH0));
  xor xor_1 (xor_1_out, Aout, nA);
  xor xor_2 (xor_2_out, Bout, nB);
  nand nand_4 (SetC_t, T1, C);
  nand nand_5 (nand_5_out, C, C);
  Seven_Seg_Hex seven_seg_hex_1 (.d({A14, A13, A12, A11}), .dp(1'b0));
  nand nand_6 (ResC, nand_5_out, LD);
  nand nand_7 (CLR, CLA, LD);
  Seven_Seg_Hex seven_seg_hex_2 (.d({A10, A9, A8, A7}), .dp(1'b0));
  xor xor_3 (xor_3_out, xor_1_out, xor_2_out);
  Seven_Seg_Hex seven_seg_hex_3 (.d({A6, A5, A4, A3}), .dp(1'b0));
  Seven_Seg_Hex seven_seg_hex_4 (.d({A2, A1, A0, nPH0}), .dp(1'b0));
  xor xor_4 (xor_4_out, xor_3_out, Cin);
  nand nand_8 (nand_8_out, xor_3_out, Cin);
  nand nand_9 (nand_9_out, xor_1_out, xor_2_out);
  Seven_Seg_Hex seven_seg_hex_5 (.d({IR7, IR6, IR5, IR4}), .dp(1'b0));
  nand nand_10 (nand_10_out, nand_8_out, nand_9_out);
  Seven_Seg_Hex seven_seg_hex_6 (.d({IR3, IR2, IR1, IR0}), .dp(1'b0));
  nand nand_11 (nand_11_out, xor_4_out, I0);
  nand nand_12 (nand_12_out, I1, nand_10_out);
  nand nand_13 (nand_13_out, nand_10_out, F);
  Seven_Seg_Hex seven_seg_hex_7 (.d({DAT7, DAT6, DAT5, DAT4}), .dp(1'b0));
  Seven_Seg_Hex seven_seg_hex_8 (.d({DAT3, DAT2, DAT1, DAT0}), .dp(1'b0));
  nand nand_14 (Sum, nand_11_out, nand_12_out);
  nand nand_15 (Carry, nand_13_out, nand_13_out);
  _7474 U19 (
    .pin1(ResC), .pin2(Carry), .pin3(GCLK), .pin4(SetC_t), .pin5(Cin), .pin7(1'b0), .pin10(1'b1),
    .pin11(1'b1), .pin12(1'b1), .pin13(1'b1), .pin14(1'b1));  // open: pin6, pin8, pin9
  Seven_Seg_Hex seven_seg_hex_9 (.d({BUS7, BUS6, BUS5, BUS4}), .dp(1'b0));
  Seven_Seg_Hex seven_seg_hex_10 (.d({BUS3, BUS2, BUS1, BUS0}), .dp(1'b0));
  LED u_CARRY (.in(Cin));
  Seven_Seg_Hex seven_seg_hex_11 (.d({PL7, PL6, PL5, PL4}), .dp(1'b0));
  Seven_Seg_Hex seven_seg_hex_12 (.d({PL3, PL2, PL1, PL0}), .dp(1'b0));
  Seven_Seg_Hex seven_seg_hex_13 (.d({RA3, RA2, RA1, RA0}), .dp(1'b0));
  _74165 U11 (
    .pin1(nPH1), .pin2(GCLK), .pin3(BUS3), .pin4(BUS2), .pin5(BUS1), .pin6(BUS0), .pin8(1'b0), .pin9(Bout),
    .pin10(1'b0), .pin11(BUS7), .pin12(BUS6), .pin13(BUS5), .pin14(BUS4), .pin15(1'b0), .pin16(1'b1));  // open: pin7
  _74595 U10 (
    .pin1(PL6), .pin2(PL5), .pin3(PL4), .pin4(PL3), .pin5(PL2), .pin6(PL1), .pin7(PL0), .pin8(1'b0),
    .pin9(Aout), .pin10(nT1), .pin11(GCLK), .pin12(ACLK), .pin13(nACOE), .pin14(Bout), .pin15(PL7),
    .pin16(1'b1));
  _74138 U20 (
    .pin1(IR4), .pin2(IR5), .pin3(IR6), .pin4(1'b0), .pin5(1'b0), .pin6(1'b1), .pin7(nJMP), .pin8(1'b0),
    .pin9(U20_pin9), .pin10(U20_pin10), .pin11(U20_pin11), .pin12(U20_pin12), .pin13(U20_pin13),
    .pin14(U20_pin14), .pin15(U20_pin15), .pin16(1'b1));
  LED u_LOAD (.in(LOAD));
  LED AND_4 (.in(AND));
  LED OR_2 (.in(OR));
  LED XOR_5 (.in(XOR));
  LED u_ADD (.in(ADD));
  LED u_SUB (.in(SUB));
  LED STORE (.in(ST));
  LED JUMP (.in(JMP));
  DiodeBackward diodebackward_1 (.in(U20_pin15), .out(diodebackward_1_out));
  PullUp pullup_7 (.out(pullup_7_out));
  PullUp pullup_8 (.out(diodebackward_1_out));
  DiodeBackward diodebackward_2 (.in(U20_pin15), .out(pullup_7_out));
  DiodeBackward diodebackward_3 (.in(U20_pin11), .out(pullup_7_out));
  DiodeBackward diodebackward_4 (.in(U20_pin10), .out(pullup_7_out));
  DiodeBackward diodebackward_5 (.in(nJMP), .out(pullup_7_out));
  PullUp pullup_9 (.out(pullup_9_out));
  DiodeBackward diodebackward_6 (.in(U20_pin10), .out(diodebackward_6_out));
  DiodeBackward diodebackward_7 (.in(U20_pin10), .out(pullup_9_out));
  PullUp pullup_10 (.out(diodebackward_6_out));
  DiodeBackward diodebackward_8 (.in(nJMP), .out(diodebackward_8_out));
  _74595 U22 (
    .pin1(BUS6), .pin2(BUS5), .pin3(BUS4), .pin4(BUS3), .pin5(BUS2), .pin6(BUS1), .pin7(BUS0), .pin8(1'b0),
    .pin9(Aout), .pin10(nT1), .pin11(GCLK), .pin12(ACLK), .pin13(nACOE), .pin14(Sum), .pin15(BUS7),
    .pin16(1'b1));
  PullUp pullup_11 (.out(diodebackward_8_out));
  PullUp pullup_12 (.out(pullup_12_out));
  DiodeBackward diodebackward_9 (.in(U20_pin14), .out(pullup_12_out));
  DiodeBackward diodebackward_10 (.in(U20_pin13), .out(pullup_12_out));
  PullUp pullup_13 (.out(pullup_13_out));
  DiodeBackward diodebackward_11 (.in(U20_pin15), .out(pullup_13_out));
  DiodeBackward diodebackward_12 (.in(U20_pin13), .out(pullup_13_out));
  DiodeBackward diodebackward_13 (.in(U20_pin12), .out(pullup_13_out));
  DiodeBackward diodebackward_14 (.in(U20_pin11), .out(pullup_13_out));
  DiodeBackward diodebackward_15 (.in(U20_pin10), .out(pullup_13_out));
  DiodeBackward diodebackward_16 (.in(U20_pin9), .out(pullup_13_out));
  DiodeBackward diodebackward_17 (.in(nJMP), .out(pullup_13_out));
  _74540 U24 (
    .pin1(1'b0), .pin2(U20_pin15), .pin3(U20_pin14), .pin4(U20_pin13), .pin5(U20_pin12), .pin6(U20_pin11),
    .pin7(U20_pin10), .pin8(U20_pin9), .pin9(nJMP), .pin10(1'b0), .pin11(JMP), .pin12(ST), .pin13(SUB),
    .pin14(ADD), .pin15(XOR), .pin16(OR), .pin17(AND), .pin18(LOAD), .pin19(1'b0), .pin20(1'b1));
  _74540 U21 (
    .pin1(1'b0), .pin2(pullup_13_out), .pin3(pullup_12_out), .pin4(diodebackward_8_out),
    .pin5(diodebackward_6_out), .pin6(pullup_9_out), .pin7(pullup_7_out), .pin8(diodebackward_1_out),
    .pin9(Zin), .pin10(1'b0), .pin11(ZERO), .pin12(CLA), .pin13(F), .pin14(C), .pin15(nB), .pin16(nA),
    .pin17(I1), .pin18(I0), .pin19(1'b0), .pin20(1'b1));
  DiodeForward diodeforward_1 (.in(BUS7), .out(Zin));
  DiodeForward diodeforward_2 (.in(BUS6), .out(Zin));
  DiodeForward diodeforward_3 (.in(BUS5), .out(Zin));
  DiodeForward diodeforward_4 (.in(BUS4), .out(Zin));
  DiodeForward diodeforward_5 (.in(BUS3), .out(Zin));
  DiodeForward diodeforward_6 (.in(BUS2), .out(Zin));
  DiodeForward diodeforward_7 (.in(BUS1), .out(Zin));
  DiodeForward diodeforward_8 (.in(BUS0), .out(Zin));
  Seven_Seg_Hex seven_seg_hex_14 (.d({BUS7, BUS6, BUS5, BUS4}), .dp(1'b0));
  PullDown pulldown_2 (.out(Zin));
  Seven_Seg_Hex seven_seg_hex_15 (.d({BUS3, BUS2, BUS1, BUS0}), .dp(1'b0));
  Seven_Seg_Hex seven_seg_hex_16 (.d({1'b0, CLA, F, C}), .dp(1'b0));
  LED led_11 (.in(ZERO));
  Seven_Seg_Hex seven_seg_hex_17 (.d({nB, nA, I1, I0}), .dp(1'b0));

  assign CLK = clk_2;

  // Other names for the same wires on the sheet: A0_t = nPH0; Cout = Carry; Fout = Sum; nBLD = nPH1; nLD = T0;
  //   nLOAD = T0; nRES = T1; SETC = T1; nRES_FF = nCLRPC; nT0 = LD; S0 = IR0; S1 = IR1; S2 = IR2; S3 = IR3; S4 = IR4;
  //   WR_CLK = nWR

  // Notes on the sheet:
  //   in_2: default 1
  //   clk_2: Hz: 2
  //   MITE 8-bit  Bit serial CPU Testbed
  //   10 Pulse 4017 Sequencer
  //   Select Reg
  //   U2
  //   U18A
  //   U18B
  //   74HC02
  //   U18C
  //   U18D
  //   Program Counter
  //   PROGRAM COUNTER
  //   ALU
  //   CLR ACC
  //   U14A
  //   U14B
  //   U17A
  //   U17B
  //   U17D
  //   U17C
  //   U14C
  //   Carry is only set before Bit 0 of an operation
  //   Any residual carry is cleared before an operation
  //   5 Package Bit Serial ALU
  //   U14D
  //   U15A
  //   U15B
  //   U15C
  //   INSTR
  //   Carry FF
  //   U16A
  //   U16B
  //   Suppress Carry
  //   U15D
  //   RAM DATA
  //   U16C
  //   U16D
  //   RAM BUS
  //   DATA
  //   Instruction Input
  //   8-bit Shift Register A
  //   REG
  //   8-bit Shift Register B
  //   Instruction Decode
  //   F
  //   CLA
  //   C
  //   ~B
  //   I1
  //   ~A
  //   Output Shift Register O
  //   I0
  //   LOAD
  //   AND
  //   OR
  //   XOR
  //   ADD
  //   SUB
  //   STORE
  //   JMP
  //   OUTPUT
  //   ZERO
endmodule
