// Digital circuit MITE_Spain_3.dig as structural Verilog
module MITE_Spain_3 (
  input  clk,
  input  IR5,
  input  IR6,
  input  IR7,
  input  S0,
  input  S1,
  input  S2,
  input  SetC,
  input  in_13,
  input  S3,
  output LD,
  output RES,
  output GCLK,
  output T0
);

  wire AC0, AC1, AC2, AC3, AC4, AC5, AC6, AC7, ADD, AND, Bout, button_1_out, button_2_out, button_3_out,
       button_4_out, button_5_out, button_6_out, button_7_out, button_8_out, button_9_out, button_10_out, C,
       Cin, CLA, CLR, Cout, D0, D1, D2, D3, D4, D5, D6, D7, d_ff_1_nq, d_ff_2_nq, d_ff_3_nq, d_ff_4_nq,
       d_ff_5_nq, d_ff_6_nq, diodebackward_1_out, diodebackward_2_out, diodebackward_8_out,
       diodebackward_9_out, F, Fout, I0, I1, IC16_2_nq, IC16_nq, LD_t, LOAD, nA, nand_1_out, nand_3_out,
       nand_4_out, nand_5_out, nand_6_out, nand_7_out, nand_8_out, nand_9_out, nand_10_out, nand_13_out,
       nand_15_out, nB, nCLRPC, nJMP, OR, pullup_2_out, pullup_4_out, pullup_7_out, SETC_t, ST, SUB,
       U2_pin14, UP, XOR, xor_1_out, xor_2_out, xor_3_out, xor_4_out;
  wire [3:0] U7_pin3;

  Monoflop monoflop_1 (.C(LD), .R(1'b0), .Q(SETC_t), .nQ(RES));
  Monoflop monoflop_2 (.C(button_1_out), .R(1'b0), .Q(LD_t), .nQ(LD));
  Button button_1 (.out(button_1_out));
  _74138 U1 (
    .pin1(IR5), .pin2(IR6), .pin3(IR7), .pin4(1'b0), .pin5(1'b0), .pin6(1'b1), .pin7(nJMP), .pin8(1'b0),
    .pin9(ST), .pin10(SUB), .pin11(ADD), .pin12(XOR), .pin13(OR), .pin14(AND), .pin15(LOAD), .pin16(1'b1));
  DiodeBackward diodebackward_1 (.in(LOAD), .out(diodebackward_1_out));
  PullUp pullup_1 (.out(diodebackward_1_out));
  DiodeBackward diodebackward_2 (.in(LOAD), .out(diodebackward_2_out));
  DiodeBackward diodebackward_3 (.in(ADD), .out(diodebackward_2_out));
  DiodeBackward diodebackward_4 (.in(SUB), .out(diodebackward_2_out));
  DiodeBackward diodebackward_5 (.in(nJMP), .out(diodebackward_2_out));
  Monoflop monoflop_3 (.C(button_2_out), .R(1'b0), .nQ(nCLRPC));  // open: Q
  Button button_2 (.out(button_2_out));
  PullUp pullup_2 (.out(pullup_2_out));
  PullUp pullup_3 (.out(diodebackward_2_out));
  DiodeBackward diodebackward_6 (.in(SUB), .out(pullup_2_out));
  PullUp pullup_4 (.out(pullup_4_out));
  DiodeBackward diodebackward_7 (.in(SUB), .out(pullup_4_out));
  DiodeBackward diodebackward_8 (.in(nJMP), .out(diodebackward_8_out));
  PullUp pullup_5 (.out(diodebackward_8_out));
  DiodeBackward diodebackward_9 (.in(AND), .out(diodebackward_9_out));
  DiodeBackward diodebackward_10 (.in(OR), .out(diodebackward_9_out));
  PullUp pullup_6 (.out(diodebackward_9_out));
  PullUp pullup_7 (.out(pullup_7_out));
  DiodeBackward diodebackward_11 (.in(LOAD), .out(pullup_7_out));
  DiodeBackward diodebackward_12 (.in(OR), .out(pullup_7_out));
  DiodeBackward diodebackward_13 (.in(XOR), .out(pullup_7_out));
  DiodeBackward diodebackward_14 (.in(ADD), .out(pullup_7_out));
  DiodeBackward diodebackward_15 (.in(SUB), .out(pullup_7_out));
  DiodeBackward diodebackward_16 (.in(ST), .out(pullup_7_out));
  DiodeBackward diodebackward_17 (.in(nJMP), .out(pullup_7_out));
  _74540 U2 (
    .pin1(1'b0), .pin2(pullup_7_out), .pin3(diodebackward_9_out), .pin4(diodebackward_8_out),
    .pin5(pullup_4_out), .pin6(pullup_2_out), .pin7(diodebackward_2_out), .pin8(diodebackward_1_out),
    .pin9(1'b0), .pin10(1'b0), .pin12(CLA), .pin13(F), .pin14(U2_pin14), .pin15(nB), .pin16(nA), .pin17(I1),
    .pin18(I0), .pin19(1'b0), .pin20(1'b1));  // open: pin11
  or or_1 (C, U2_pin14, SetC);
  Seven_Seg_Hex seven_seg_hex_1 (.d({AC7, AC6, AC5, AC4}), .dp(1'b0));
  _74164 U3 (
    .pin1(1'b1), .pin2(Fout), .pin3(AC7), .pin4(AC6), .pin5(AC5), .pin6(AC4), .pin7(1'b0), .pin8(GCLK),
    .pin9(CLR), .pin10(AC3), .pin11(AC2), .pin12(AC1), .pin13(AC0), .pin14(1'b1));
  Seven_Seg_Hex seven_seg_hex_2 (.d({AC3, AC2, AC1, AC0}), .dp(1'b0));
  LED led_1 (.in(D7));
  D_FF IC16 (.D(IC16_nq), .C(button_3_out), .Q(D7), .nQ(IC16_nq));
  LED led_2 (.in(D6));
  D_FF d_ff_1 (.D(d_ff_1_nq), .C(button_4_out), .Q(D6), .nQ(d_ff_1_nq));
  Button button_3 (.out(button_3_out));
  _74165 U4 (
    .pin1(LD), .pin2(GCLK), .pin3(D3), .pin4(D2), .pin5(D1), .pin6(D0), .pin8(1'b0), .pin9(Bout),
    .pin10(1'b0), .pin11(D7), .pin12(D6), .pin13(D5), .pin14(D4), .pin15(1'b0), .pin16(1'b1));  // open: pin7
  LED led_3 (.in(D5));
  D_FF d_ff_2 (.D(d_ff_2_nq), .C(button_5_out), .Q(D5), .nQ(d_ff_2_nq));
  Button button_4 (.out(button_4_out));
  LED led_4 (.in(D4));
  D_FF d_ff_3 (.D(d_ff_3_nq), .C(button_6_out), .Q(D4), .nQ(d_ff_3_nq));
  Button button_5 (.out(button_5_out));
  LED led_5 (.in(D3));
  D_FF d_ff_4 (.D(d_ff_4_nq), .C(button_7_out), .Q(D3), .nQ(d_ff_4_nq));
  Button button_6 (.out(button_6_out));
  LED led_6 (.in(D2));
  D_FF d_ff_5 (.D(d_ff_5_nq), .C(button_8_out), .Q(D2), .nQ(d_ff_5_nq));
  Button button_7 (.out(button_7_out));
  LED led_7 (.in(D1));
  D_FF d_ff_6 (.D(d_ff_6_nq), .C(button_9_out), .Q(D1), .nQ(d_ff_6_nq));
  Button button_8 (.out(button_8_out));
  LED led_8 (.in(D0));
  D_FF IC16_2 (.D(IC16_2_nq), .C(button_10_out), .Q(D0), .nQ(IC16_2_nq));
  Button button_9 (.out(button_9_out));
  Seven_Seg_Hex seven_seg_hex_3 (.d({D7, D6, D5, D4}), .dp(1'b0));
  Button button_10 (.out(button_10_out));
  Seven_Seg_Hex seven_seg_hex_4 (.d({D3, D2, D1, D0}), .dp(1'b0));
  xor xor_1 (xor_1_out, AC0, nA);
  xor xor_2 (xor_2_out, nB, Bout);
  nand nand_1 (nand_1_out, SETC_t, C);
  nand nand_2 (CLR, CLA, LD_t);
  nand nand_3 (nand_3_out, C, C);
  Seven_Seg_Hex seven_seg_hex_5 (.d(U7_pin3), .dp(1'b0));
  nand nand_4 (nand_4_out, nand_3_out, LD_t);
  xor xor_3 (xor_3_out, xor_1_out, xor_2_out);
  xor xor_4 (xor_4_out, xor_3_out, Cin);
  nand nand_5 (nand_5_out, xor_3_out, Cin);
  nand nand_6 (nand_6_out, xor_1_out, xor_2_out);
  _74193 U7 (
    .pin1(S1), .pin2(U7_pin3[1]), .pin3(U7_pin3[0]), .pin4(GCLK), .pin5(1'b1), .pin6(U7_pin3[2]),
    .pin7(U7_pin3[3]), .pin8(1'b0), .pin9(1'b0), .pin10(S2), .pin11(RES), .pin13(T0), .pin14(in_13),
    .pin15(S0), .pin16(1'b1));  // open: pin12
  nand nand_7 (nand_7_out, nand_5_out, nand_6_out);
  nand nand_8 (nand_8_out, xor_4_out, I0);
  nand nand_9 (nand_9_out, I1, nand_7_out);
  nand nand_10 (nand_10_out, nand_7_out, F);
  nand nand_11 (Fout, nand_8_out, nand_9_out);
  nand nand_12 (Cout, nand_10_out, nand_10_out);
  nand nand_13 (nand_13_out, clk, clk);
  nand nand_14 (UP, RES, nand_15_out);
  nand nand_15 (nand_15_out, UP, T0);
  nand nand_16 (GCLK, nand_13_out, UP);
  _7474 U12 (
    .pin1(nand_4_out), .pin2(Cout), .pin3(GCLK), .pin4(nand_1_out), .pin5(Cin), .pin7(1'b0), .pin10(1'b1),
    .pin11(clk), .pin12(1'b1), .pin13(1'b1), .pin14(1'b1));  // open: pin6, pin8, pin9

  // Other names for the same wires on the sheet: Aout = AC0; nLOAD = LD; nRES = RES; nSET = T0; S4 = SetC

  // Notes on the sheet:
  //   clk: Hz: 2
  //   S0: default 1
  //   S1: default 1
  //   S2: default 1
  //   MITE 8-bit Test Bed
  //   Instruction Input
  //   STEP/RUN
  //   CLR PC
  //   Instruction Decode
  //   CLA
  //   C
  //   F
  //   ~B
  //   ~A
  //   I0
  //   I1
  //   LOAD
  //   AND
  //   OR
  //   XOR
  //   ADD
  //   SUB
  //   STORE
  //   JMP
  //   8-bit Shift Register A
  //   ACCUMULATOR
  //   8-bit Shift Register B
  //   Data Input
  //   Sequencer
  //   ******Shift Operations******
  //   S Field  	Operation
  //   0000	Left Shift 7
  //   0001	Left Shift 6
  //   0010	Left Shift 5
  //   0011	Left Shift 4
  //   0100	Left Shift 3
  //   0101	Left Shift 2
  //   0110	Left Shift 1	
  //   0111	No Shift	8-bit transfer
  //   1000	Right Shift 1
  //   1001	Right Shift 2
  //   1010	Right Shift 3		
  //   1011	Nybble Swap (bit shift)
  //   1100	Left Shift 3
  //   1101	Left Shift 2
  //   1110	No Shift 16-bit transfer
  //   1111	No Shift
  //   ALU
  //   CLR ACC
  //   # Clock
  //   Variable Pulse Train Clock Sequencer
  //   Input (15-S) Pulses
  //   MITE 8-bit  Bit serial CPU Testbed
  //   Carry is only set before Bit 0 of an operation
  //   Any residual carry is cleared before an operation
  //   Suppress Carry
  //   U8
  //   Carry FF
endmodule
