// Digital circuit MITE_Spain_9.dig as structural Verilog
module MITE_Spain_9 (
  input  in_1,
  input  in_5,
  input  in_6,
  input  clk,
  input  in_24,
  input  S2,
  input  S1,
  input  S0,
  output SETC,
  output GCLK,
  output LOAD,
  output T9,
  output T8,
  output T7,
  output T6,
  output T5,
  output T4,
  output T3,
  output T2,
  output T1,
  output T0,
  output GCLK_2,
  output CLR,
  output LD,
  output RES,
  output GCLK_3,
  output T10
);

  wire _74161_1_pin10, A0, A1, A2, A3, A4, A5, A6, A7, A8, A9, A10, A11, A12, A13, A14, A15, ADD, AND, Aout,
       Bout, button_1_out, button_2_out, button_3_out, button_4_out, button_5_out, button_6_out,
       button_7_out, button_8_out, C, CC, Cin, CLA, Cout, D0, D1, D2, D3, D4, D5, D6, D7, d_ff_1_nq,
       d_ff_2_nq, d_ff_3_nq, d_ff_4_nq, d_ff_5_nq, d_ff_6_nq, F, Fout, GATE, I0, I1, IC16_2_nq, IC16_nq,
       INCPC, IR0, IR1, IR2, IR3, IR4, IR5, IR6, IR7, K0, K1, K2, K3, K4, K5, K6, K7, LOAD_t, nA, nand_1_out,
       nand_2_out, nand_3_out, nand_5_out, nand_6_out, nand_8_out, nand_9_out, nand_10_out, nand_11_out,
       nand_12_out, nand_13_out, nand_14_out, nand_17_out, nand_19_out, nand_20_out, nB, nCLRPC, nJMP,
       nor_3_out, nor_4_out, not_1_out, not_2_out, nSET, OR, PC_Carry, PC_Cin, PCin, PCout, PL0, PL1, PL2,
       PL3, PL4, PL5, PL6, PL7, R0, R1, R2, R3, R4, R5, R6, RES_t, ST, ST0, ST1, SUB, U8_p16, UP, XOR,
       xor_1_out, xor_3_out, xor_4_out, xor_5_out, xor_6_out, xor_7_out;
  wire [3:0] U7_2_pin3;

  _744017 U11 (
    .pin1(T5), .pin2(T1), .pin3(T0), .pin4(T2), .pin5(T6), .pin6(T7), .pin7(T3), .pin8(1'b0), .pin9(T8),
    .pin10(T4), .pin11(T9), .pin13(1'b0), .pin14(clk), .pin15(1'b0), .pin16(1'b1));  // open: pin12
  Monoflop monoflop_1 (.C(T0), .R(1'b0), .Q(LD), .nQ(LOAD));
  not not_1 (not_1_out, T0);
  PullUp pullup_1 (.out(IR4));
  Reset reset_1 (.out(nCLRPC));
  Monoflop monoflop_2 (.C(LOAD), .R(1'b0), .Q(RES), .nQ(RES_t));
  _74138 U1 (
    .pin1(IR5), .pin2(IR6), .pin3(IR7), .pin4(1'b0), .pin5(1'b0), .pin6(1'b1), .pin7(nJMP), .pin8(1'b0),
    .pin9(ST), .pin10(SUB), .pin11(ADD), .pin12(XOR), .pin13(OR), .pin14(AND), .pin15(LOAD_t), .pin16(1'b1));
  PullUp pullup_2 (.out(IR3));
  PullUp pullup_3 (.out(IR2));
  PullUp pullup_4 (.out(IR1));
  PullUp pullup_5 (.out(IR0));
  DiodeBackward diodebackward_1 (.in(LOAD_t), .out(R6));
  nor nor_1 (GCLK_2, GATE, clk);
  nor nor_2 (GATE, T1, nor_3_out);
  nor nor_3 (nor_3_out, GATE, T9);
  PullUp pullup_6 (.out(R5));
  PullUp pullup_7 (.out(R6));
  DiodeBackward diodebackward_2 (.in(LOAD_t), .out(R5));
  DiodeBackward diodebackward_3 (.in(ADD), .out(R5));
  DiodeBackward diodebackward_4 (.in(SUB), .out(R5));
  DiodeBackward diodebackward_5 (.in(nJMP), .out(R5));
  // _28c256 U8: pin names not known; wires that end beside it: A14, A12, A7, A6, A5, A4, A3, A2, A1, T0, D0, D1, D2, 1'b0, 1'b1, U8_p16, A13, A8, A9, A11, in_5, A10, 1'b0, D7
  PullUp pullup_8 (.out(R4));
  DiodeBackward diodebackward_6 (.in(SUB), .out(R3));
  DiodeBackward diodebackward_7 (.in(SUB), .out(R4));
  PullUp pullup_9 (.out(R3));
  DiodeBackward diodebackward_8 (.in(nJMP), .out(R2));
  PullUp pullup_10 (.out(R2));
  PullUp pullup_11 (.out(R1));
  DiodeBackward diodebackward_9 (.in(AND), .out(R1));
  DiodeBackward diodebackward_10 (.in(OR), .out(R1));
  PullUp pullup_12 (.out(R0));
  DiodeBackward diodebackward_11 (.in(LOAD_t), .out(R0));
  DiodeBackward diodebackward_12 (.in(OR), .out(R0));
  DiodeBackward diodebackward_13 (.in(XOR), .out(R0));
  DiodeBackward diodebackward_14 (.in(ADD), .out(R0));
  DiodeBackward diodebackward_15 (.in(SUB), .out(R0));
  DiodeBackward diodebackward_16 (.in(ST), .out(R0));
  DiodeBackward diodebackward_17 (.in(nJMP), .out(R0));
  _7474 U2 (
    .pin1(1'b1), .pin2(ST1), .pin3(T0), .pin4(1'b1), .pin5(ST0), .pin6(ST1), .pin7(1'b0), .pin9(PC_Cin),
    .pin10(LOAD), .pin11(GCLK_2), .pin12(PC_Carry), .pin13(1'b1), .pin14(1'b1));  // open: pin8
  PullUp pullup_13 (.out(U8_p16));
  PullUp pullup_14 (.out(in_5));
  nor nor_4 (nor_4_out, CC, IR4);
  and and_1 (INCPC, A7, A6, A5, A4, A3, A2, A1, A0);
  _74574 _74574_1 (
    .pin1(ST0), .pin2(D7), .pin3(D6), .pin4(D5), .pin5(D4), .pin6(D3), .pin7(D2), .pin8(D1), .pin9(D0),
    .pin10(1'b0), .pin11(T0), .pin12(IR0), .pin13(IR1), .pin14(IR2), .pin15(IR3), .pin16(IR4), .pin17(IR5),
    .pin18(IR6), .pin19(IR7), .pin20(1'b1));
  _74540 U2_2 (
    .pin1(1'b0), .pin2(R0), .pin3(R1), .pin4(R2), .pin5(R3), .pin6(R4), .pin7(R5), .pin8(R6),
    .pin9(nor_4_out), .pin10(1'b0), .pin11(C), .pin12(CLA), .pin13(F), .pin14(CC), .pin15(nB), .pin16(nA),
    .pin17(I1), .pin18(I0), .pin19(1'b0), .pin20(1'b1));
  _74541 _74541_1 (
    .pin1(1'b1), .pin2(K7), .pin3(K6), .pin4(K5), .pin5(K4), .pin6(K3), .pin7(K2), .pin8(K1), .pin9(K0),
    .pin10(1'b0), .pin11(D0), .pin12(D1), .pin13(D2), .pin14(D3), .pin15(D4), .pin16(D5), .pin17(D6),
    .pin18(D7), .pin19(1'b1), .pin20(1'b1));
  LED led_1 (.in(K7));
  D_FF IC16 (.D(IC16_nq), .C(button_1_out), .Q(K7), .nQ(IC16_nq));
  Button button_1 (.out(button_1_out));
  _74161 _74161_1 (
    .pin1(1'b1), .pin2(INCPC), .pin3(1'b0), .pin4(1'b0), .pin5(1'b0), .pin6(1'b0), .pin7(1'b1), .pin8(1'b0),
    .pin9(1'b1), .pin10(_74161_1_pin10), .pin11(A15), .pin12(A14), .pin13(A13), .pin14(A12), .pin16(1'b1));  // open: pin15
  _74161 _74161_2 (
    .pin1(1'b1), .pin2(INCPC), .pin3(1'b0), .pin4(1'b0), .pin5(1'b0), .pin6(1'b0), .pin7(1'b1), .pin8(1'b0),
    .pin9(1'b1), .pin10(1'b1), .pin11(A11), .pin12(A10), .pin13(A9), .pin14(A8), .pin15(_74161_1_pin10),
    .pin16(1'b1));
  LED led_2 (.in(K6));
  D_FF d_ff_1 (.D(d_ff_1_nq), .C(button_2_out), .Q(K6), .nQ(d_ff_1_nq));
  Button button_2 (.out(button_2_out));
  xor xor_1 (xor_1_out, PCout, PC_Cin);
  nand nand_1 (nand_1_out, PCout, PC_Cin);
  LED led_3 (.in(K5));
  D_FF d_ff_2 (.D(d_ff_2_nq), .C(button_3_out), .Q(K5), .nQ(d_ff_2_nq));
  Button button_3 (.out(button_3_out));
  LED led_4 (.in(K4));
  D_FF d_ff_3 (.D(d_ff_3_nq), .C(button_4_out), .Q(K4), .nQ(d_ff_3_nq));
  Button button_4 (.out(button_4_out));
  xor xor_2 (PC_Carry, 1'b1, nand_1_out);
  LED led_5 (.in(K3));
  D_FF d_ff_4 (.D(d_ff_4_nq), .C(button_5_out), .Q(K3), .nQ(d_ff_4_nq));
  Button button_5 (.out(button_5_out));
  xor xor_3 (xor_3_out, 1'b1, in_1);
  not not_2 (not_2_out, T0);
  LED led_6 (.in(K2));
  D_FF d_ff_5 (.D(d_ff_5_nq), .C(button_6_out), .Q(K2), .nQ(d_ff_5_nq));
  Button button_6 (.out(button_6_out));
  _74595 U8_2 (
    .pin1(PL6), .pin2(PL5), .pin3(PL4), .pin4(PL3), .pin5(PL2), .pin6(PL1), .pin7(PL0), .pin8(1'b0),
    .pin9(Aout), .pin10(CLR), .pin11(GCLK), .pin12(T9), .pin13(ST0), .pin14(Fout), .pin15(PL7), .pin16(1'b1));
  _74165 U4 (
    .pin1(not_2_out), .pin2(GCLK), .pin3(D3), .pin4(D2), .pin5(D1), .pin6(D0), .pin8(1'b0), .pin9(Bout),
    .pin10(1'b0), .pin11(D7), .pin12(D6), .pin13(D5), .pin14(D4), .pin15(1'b0), .pin16(1'b1));  // open: pin7
  LED led_7 (.in(K1));
  D_FF d_ff_6 (.D(d_ff_6_nq), .C(button_7_out), .Q(K1), .nQ(d_ff_6_nq));
  Button button_7 (.out(button_7_out));
  nand nand_2 (nand_2_out, xor_1_out, xor_3_out);
  nand nand_3 (nand_3_out, in_1, in_6);
  LED led_8 (.in(K0));
  D_FF IC16_2 (.D(IC16_2_nq), .C(button_8_out), .Q(K0), .nQ(IC16_2_nq));
  Button button_8 (.out(button_8_out));
  nand nand_4 (PCin, nand_2_out, nand_3_out);
  Seven_Seg_Hex seven_seg_hex_1 (.d({K7, K6, K5, K4}), .dp(1'b0));
  Seven_Seg_Hex seven_seg_hex_2 (.d({K3, K2, K1, K0}), .dp(1'b0));
  xor xor_4 (xor_4_out, Aout, nA);
  xor xor_5 (xor_5_out, nB, Bout);
  nand nand_5 (nand_5_out, RES, C);
  nand nand_6 (nand_6_out, C, C);
  nand nand_7 (CLR, CLA, LOAD);
  _74595 U7 (
    .pin1(A6), .pin2(A5), .pin3(A4), .pin4(A3), .pin5(A2), .pin6(A1), .pin7(A0), .pin8(1'b0), .pin9(PCout),
    .pin10(nCLRPC), .pin11(GCLK_2), .pin12(T9), .pin13(1'b0), .pin14(PCin), .pin15(A7), .pin16(1'b1));
  xor xor_6 (xor_6_out, xor_4_out, xor_5_out);
  nand nand_8 (nand_8_out, nand_6_out, LOAD);
  Seven_Seg_Hex seven_seg_hex_3 (.d(U7_2_pin3), .dp(1'b0));
  xor xor_7 (xor_7_out, xor_6_out, Cin);
  nand nand_9 (nand_9_out, xor_6_out, Cin);
  nand nand_10 (nand_10_out, xor_4_out, xor_5_out);
  Seven_Seg_Hex seven_seg_hex_4 (.d({A15, A14, A13, A12}), .dp(1'b0));
  nand nand_11 (nand_11_out, nand_9_out, nand_10_out);
  Seven_Seg_Hex seven_seg_hex_5 (.d({A11, A10, A9, A8}), .dp(1'b0));
  _74193 U7_2 (
    .pin1(S1), .pin2(U7_2_pin3[1]), .pin3(U7_2_pin3[0]), .pin4(GCLK), .pin5(1'b1), .pin6(U7_2_pin3[2]),
    .pin7(U7_2_pin3[3]), .pin8(1'b0), .pin9(1'b0), .pin10(S2), .pin11(RES), .pin13(nSET), .pin14(in_24),
    .pin15(S0), .pin16(1'b1));  // open: pin12
  Seven_Seg_Hex seven_seg_hex_6 (.d({A7, A6, A5, A4}), .dp(1'b0));
  nand nand_12 (nand_12_out, xor_7_out, I0);
  nand nand_13 (nand_13_out, I1, nand_11_out);
  nand nand_14 (nand_14_out, nand_11_out, F);
  Seven_Seg_Hex seven_seg_hex_7 (.d({A3, A2, A1, A0}), .dp(1'b0));
  nand nand_15 (Fout, nand_12_out, nand_13_out);
  nand nand_16 (Cout, nand_14_out, nand_14_out);
  Seven_Seg_Hex seven_seg_hex_8 (.d({IR7, IR6, IR5, IR4}), .dp(1'b0));
  Seven_Seg_Hex seven_seg_hex_9 (.d({IR3, IR2, IR1, IR0}), .dp(1'b0));
  nand nand_17 (nand_17_out, clk, clk);
  nand nand_18 (UP, RES, nand_19_out);
  nand nand_19 (nand_19_out, UP, nSET);
  Seven_Seg_Hex seven_seg_hex_10 (.d({PL7, PL6, PL5, PL4}), .dp(1'b0));
  _7474 U12 (
    .pin1(nand_8_out), .pin2(Cout), .pin3(GCLK), .pin4(nand_5_out), .pin5(Cin), .pin7(1'b0), .pin10(1'b1),
    .pin11(clk), .pin12(1'b1), .pin13(1'b1), .pin14(1'b1));  // open: pin6, pin8, pin9
  Seven_Seg_Hex seven_seg_hex_11 (.d({PL3, PL2, PL1, PL0}), .dp(1'b0));
  nand nand_20 (nand_20_out, nand_17_out, UP);
  not not_3 (GCLK, nand_20_out);
  LED led_9 (.in(T9));
  LED led_10 (.in(T8));
  LED led_11 (.in(T7));
  LED led_12 (.in(T6));
  LED led_13 (.in(T5));
  LED led_14 (.in(T4));
  LED led_15 (.in(T3));
  LED led_16 (.in(T2));
  LED led_17 (.in(T1));
  LED led_18 (.in(T0));
  LED u_ST0 (.in(ST0));
  LED u_ST1 (.in(ST1));

  assign GCLK_3 = GCLK;
  assign SETC = RES;
  assign T10 = T0;

  // Other names for the same wires on the sheet: LD_t = LOAD; nINC_LD = in_1; nLD = LD; nLOAD = LD; nRES = RES;
  //   PCCLK = GCLK_2; Rout = in_6; S0_t = IR0; S1_t = IR1; S2_t = IR2; S3 = IR3; S4 = IR4

  // Notes on the sheet:
  //   clk: Hz: 2
  //   S2: default 1
  //   S1: default 1
  //   S0: default 1
  //   8 to 10 Pulse 4017 Sequencer
  //   STEP/RUN
  //   Instruction Input
  //   U14
  //   74HC02
  //   CLA
  //   F
  //   Instruction Decode
  //   C
  //   ~A
  //   ~B
  //   I1
  //   PC Carry FF
  //   I0
  //   LOAD
  //   AND
  //   OR
  //   XOR
  //   ADD
  //   SUB
  //   STORE
  //   JMP
  //   U14D
  //   Data Input
  //   Program Counter (Incrementer)
  //   Carry is only set before Bit 0 of an operation
  //   U4A
  //   U5A
  //   U4C
  //   8-bit Shift Register A
  //   8-bit Shift Register B
  //   U4B
  //   U5C
  //   U5B
  //   U5D
  //   ******Shift Operations******
  //   S Field  	Operation
  //   0000	Left Shift 7
  //   0001	Left Shift 6
  //   0010	Left Shift 5
  //   0011	Left Shift 4
  //   0100	Left Shift 3
  //   0101	Left Shift 2
  //   0110	Left Shift 1	
  //   0111	No Shift	8-bit transfer
  //   1000	Right Shift 1
  //   1001	Right Shift 2
  //   1010	Right Shift 3		
  //   1011	Nybble Swap (bit shift)
  //   1100	Left Shift 3
  //   1101	Left Shift 2
  //   1110	No Shift 16-bit transfer
  //   1111	No Shift
  //   ALU
  //   MITE 8-bit  Bit serial CPU Testbed
  //   Sequencer
  //   # Clock
  //   Variable Pulse Train Clock Sequencer
  //   Any residual carry is cleared before an operation
  //   Input (15-S) Pulses
  //   PROGRAM COUNTER
  //   Suppress Carry
  //   U8
  //   INSTR
  //   DATA
  //   Carry FF
endmodule
